# Fritzing sketch final project circuit (saved by Fritzing 0.9.3b)
breadboards: 1

parts:
  Part1 = Arduino Uno (Rev3)
  GO_button = Pushbutton [package="[SMD]"]
  STOP_button = Pushbutton [package="[SMD]"]
  R1 = Resistor [tolerance=±5% resistance=2.2k package="1206 [SMD]"]
  R2 = Resistor [tolerance=±5% resistance=2.2k package="1206 [SMD]"]
  R3 = Resistor [tolerance=±5% resistance=560 package="1206 [SMD]"]
  LED2 = LED - 5mm [color="Red (633nm)" package="5 mm [THT]"]
  LED1 = smd LED [color="Green (560nm)" package="0603 [SMD]"]
  piezo_speaker = Piezo Speaker
  J2 = Basic Servo
  pH_meter = POT [package=pot_mammoth]
  R4 = Resistor [tolerance=±5% resistance=560 package="1206 [SMD]"]
  R5 = Resistor [tolerance=±5% resistance=560 package="1206 [SMD]"]

nets:
  N1: Part1.A4/SDA, pH_meter.A
  N2: Part1.D9_PWM, J2.pulse
  N3: Part1.D11_PWM/MOSI, piezo_speaker.pin2
  N4: Part1.D12/MISO, LED2.anode
  N5: Part1.D13/SCK, LED1.anode
  GND: Part1.GND, R1.Pin_1, R2.Pin_1, R3.Pin_1, J2.gnd, pH_meter.E, R4.Pin_1, R5.Pin_1
  N6: Part1.D6_PWM, GO_button.Pin_3, GO_button.Pin_4, R1.Pin_0
  N7: Part1.D7, STOP_button.Pin_3, STOP_button.Pin_4, R2.Pin_0
  5V: Part1.5V, GO_button.Pin_1, GO_button.Pin_2, STOP_button.Pin_1, STOP_button.Pin_2, J2.vcc, pH_meter.S
  N8: R3.Pin_0, LED1.cathode
  N9: LED2.cathode, R4.Pin_0
  N10: piezo_speaker.pin1, R5.Pin_0
